// Digital circuit Lab02.dig as structural Verilog
module Lab02 (
  input  B,
  input  C,
  input  A,
  input  D,
  output Fa,
  output Fb,
  output Fc,
  output Fd,
  output Fe,
  output Fg,
  output Ff
);

  wire AB, ACnD, AnC, BC, BD, BDnA, CD, CnA, CnB, DnB, DnC, nA, nAnC, nB, nBnD, nC, nCnD, nD;

  not not_1 (nA, A);
  not not_2 (nB, B);
  not not_3 (nC, C);
  not not_4 (nD, D);
  and and_1 (CnB, C, nB);
  and and_2 (DnB, D, nB);
  and and_3 (nAnC, nA, nC);
  and and_4 (nBnD, nB, nD);
  and and_5 (CD, C, D);
  and and_6 (BC, C, B);
  and and_7 (AnC, A, nC);
  and and_8 (DnC, D, nC);
  and and_9 (CnA, C, nA);
  and and_10 (AB, A, B);
  and and_11 (BD, D, B);
  and and_12 (nCnD, nC, nD);
  and and_13 (ACnD, A, C, nD);
  and and_14 (BDnA, nA, B, D);
  or or_1 (Fa, A, CnB, DnB);
  or or_2 (Fb, B, nAnC, ACnD);
  or or_3 (Fc, A, nBnD, CD);
  or or_4 (Fd, nBnD, BC, AnC, BDnA);
  or or_5 (Fe, DnB, DnC, CnA);
  or or_6 (Ff, CnA, nBnD, AB);
  or or_7 (Fg, A, CnB, BD, nCnD);
  Seven_Seg seven_seg_1 (.a(Fa), .b(Fb), .c(Fc), .d(Fd), .e(Fe), .f(Ff), .g(Fg), .dp(1'b0));
endmodule
