// Digital circuit add-sub.dig as structural Verilog
module add_sub (
  input  [31:0] B,
  input  [31:0] A,
  input  Sub,
  output [31:0] Out,
  output Overflow,
  output Sign
);

  wire and_1_out, and_2_out, multiplexer_2_out, multiplexer_3_out, not_33_out, not_34_out, not_35_out;
  wire [31:0] multiplexer_1_out, NOT_B;

  not not_1 (NOT_B[0], B[0]);
  not not_2 (NOT_B[1], B[1]);
  not not_3 (NOT_B[2], B[2]);
  not not_4 (NOT_B[3], B[3]);
  not not_5 (NOT_B[4], B[4]);
  not not_6 (NOT_B[5], B[5]);
  not not_7 (NOT_B[6], B[6]);
  not not_8 (NOT_B[7], B[7]);
  not not_9 (NOT_B[8], B[8]);
  not not_10 (NOT_B[9], B[9]);
  not not_11 (NOT_B[10], B[10]);
  not not_12 (NOT_B[11], B[11]);
  not not_13 (NOT_B[12], B[12]);
  not not_14 (NOT_B[13], B[13]);
  not not_15 (NOT_B[14], B[14]);
  not not_16 (NOT_B[15], B[15]);
  not not_17 (NOT_B[16], B[16]);
  not not_18 (NOT_B[17], B[17]);
  not not_19 (NOT_B[18], B[18]);
  not not_20 (NOT_B[19], B[19]);
  not not_21 (NOT_B[20], B[20]);
  not not_22 (NOT_B[21], B[21]);
  not not_23 (NOT_B[22], B[22]);
  not not_24 (NOT_B[23], B[23]);
  not not_25 (NOT_B[24], B[24]);
  not not_26 (NOT_B[25], B[25]);
  not not_27 (NOT_B[26], B[26]);
  not not_28 (NOT_B[27], B[27]);
  not not_29 (NOT_B[28], B[28]);
  not not_30 (NOT_B[29], B[29]);
  not not_31 (NOT_B[30], B[30]);
  not not_32 (NOT_B[31], B[31]);
  Multiplexer #(.Bits(32)) multiplexer_1 (.sel(Sub), .in_0(B), .in_1(NOT_B), .out(multiplexer_1_out));
  Add #(.Bits(32)) Add (.a(A), .b(multiplexer_1_out), .c_i(multiplexer_2_out), .s(Out));  // open: c_o
  Multiplexer multiplexer_2 (.sel(Sub), .in_0(1'b0), .in_1(1'b1), .out(multiplexer_2_out));
  Multiplexer multiplexer_3 (.sel(Sub), .in_0(B[31]), .in_1(NOT_B[31]), .out(multiplexer_3_out));
  and and_1 (and_1_out, A[31], multiplexer_3_out, not_33_out);
  not not_33 (not_33_out, Out[31]);
  not not_34 (not_34_out, A[31]);
  not not_35 (not_35_out, multiplexer_3_out);
  and and_2 (and_2_out, not_34_out, not_35_out, Out[31]);
  or or_1 (Overflow, and_1_out, and_2_out);

  assign Sign = Out[31];

  // Other names for the same wires on the sheet: SIGN_A = A[31]; SIGN_B = B[31]; SIGN_OUT = Out[31]
endmodule

/* Test case Add-Sub Test:
A B Sub Out Overflow Sign
0x289322C4 0x01846399 0 0x2A17865D 0 0
0x4152A22D 0x22042121 0 0x6356C34E 0 0
0x84893212 0x0994AD1A 0 0x8E1DDF2C 0 1
0x90A8826C 0x112109FB 0 0xA1C98C67 0 1
0x5210C12D 0x3D04ABBC 0 0x8F156CE9 1 1
0x90D194B5 0xB005500E 0 0x40D6E4C3 1 0
0x39332544 0x0435FCAD 1 0x34FD2897 0 0
0x59286AB1 0x221FB76C 1 0x3708B345 0 0
0xECD55935 0x248C5A4B 1 0xC848FEEA 0 1
0x902A9525 0xE5454D48 1 0xAAE547DD 0 1
0x8211036A 0x7B13890A 1 0x06FD7A60 1 0
0x5FE15DBE 0x8934B9B1 1 0xD6ACA40D 1 1
*/
